// Logisim project BabyCPU.circ as structural Verilog: 10 circuits, main circuit FullAdder
module FullAdder (
  input  Cin,
  input  A,
  input  B,
  output Sout,
  output Cout
);

  wire and_1_out, and_2_out, xor_1_out;

  and and_1 (and_1_out, A, B);
  or or_1 (Cout, and_1_out, and_2_out);
  xor xor_1 (xor_1_out, A, B);
  and and_2 (and_2_out, Cin, xor_1_out);
  xor xor_2 (Sout, Cin, xor_1_out);
endmodule

module MiniRam (
  input  A0,
  input  A1,
  input  clk,
  input  write
);

  wire and_1_out, and_2_out, and_4_out, and_7_out, and_9_out, not_1_out, not_2_out;

  not not_1 (not_1_out, A0);
  not not_2 (not_2_out, A1);
  and and_1 (and_1_out, clk, write);
  and and_2 (and_2_out, A1, A0);
  // AND_Gate and_3 has open pins: in0=and_1_out, in1=and_2_out, out=open
  and and_4 (and_4_out, A1, not_1_out);
  // AND_Gate and_5 has open pins: in0=and_1_out, in1=and_4_out, out=open
  // AND_Gate and_6 has open pins: in0=and_1_out, in1=and_7_out, out=open
  and and_7 (and_7_out, not_2_out, A0);
  // AND_Gate and_8 has open pins: in0=and_1_out, in1=and_9_out, out=open
  and and_9 (and_9_out, not_2_out, not_1_out);
endmodule

module LeftShifter (
  input  X3,
  input  X2,
  input  X1,
  input  X0,
  input  S
);

  wire and_1_out, and_2_out, and_3_out, and_4_out, and_5_out, and_6_out, and_7_out, and_8_out, not_1_out,
       not_2_out, not_3_out, not_4_out, or_1_out, or_2_out, or_3_out, or_4_out;

  not not_1 (not_1_out, S);
  and and_1 (and_1_out, not_1_out, X3);
  or or_1 (or_1_out, and_1_out, and_2_out);
  not not_2 (not_2_out, S);
  and and_2 (and_2_out, S, X2);
  and and_3 (and_3_out, not_2_out, X2);
  and and_4 (and_4_out, S, X1);
  or or_2 (or_2_out, and_3_out, and_4_out);
  not not_3 (not_3_out, S);
  and and_5 (and_5_out, not_3_out, X1);
  or or_3 (or_3_out, and_5_out, and_6_out);
  not not_4 (not_4_out, S);
  and and_6 (and_6_out, S, X0);
  and and_7 (and_7_out, not_4_out, X0);
  and and_8 (and_8_out, S, 1'b0);
  or or_4 (or_4_out, and_7_out, and_8_out);
endmodule

module Decoder3Bit (
  input  C1,
  input  C2,
  input  C3,
  input  A7,
  input  A6,
  input  A5,
  input  A4,
  input  A3,
  input  A2,
  input  A1,
  input  A0,
  output O_0,
  output O_1,
  output O_2,
  output O_3,
  output O_4,
  output O_5
);

  not not_1 (O_1, C1);
  not not_2 (O_3, C2);
  not not_3 (O_5, C3);
  and and_1 (A7, C3, C2, C1);
  and and_2 (A6, C3, C2, O_1);
  and and_3 (A5, O_5, C3, C2);
  and and_4 (A4, C3, O_3, O_1);
  and and_5 (A3, O_5, C2, C1);
  and and_6 (A2, O_5, C2, O_1);
  and and_7 (A1, O_5, O_3, C1);
  and and_8 (A0, O_5, O_3, O_1);

  assign O_0 = C1;
  assign O_2 = C2;
  assign O_4 = C3;
endmodule

module MyMultiplexer (
);

  wire A0_out, A1_out, A2_out, A3_out, A4_out, A5_out, A6_out, A7_out, and_1_out, and_2_out, and_3_out,
       and_4_out, and_5_out, and_6_out, and_7_out, and_8_out, C0_out, C1_out, C2_out, not_1_out, not_2_out,
       not_3_out, or_1_out;

  Button #(.press("passive")) C0 (.out(C0_out));
  not not_1 (not_1_out, C0_out);
  Button #(.press("passive")) C1 (.out(C1_out));
  not not_2 (not_2_out, C1_out);
  Button #(.press("passive")) C2 (.out(C2_out));
  not not_3 (not_3_out, C2_out);
  and and_1 (and_1_out, C2_out, C1_out, C0_out, A7_out);
  Button A7 (.out(A7_out));
  Button #(.press("passive")) A6 (.out(A6_out));
  and and_2 (and_2_out, C2_out, C1_out, not_1_out, A6_out);
  Button A5 (.out(A5_out));
  and and_3 (and_3_out, not_3_out, C2_out, C1_out, A5_out);
  Button A4 (.out(A4_out));
  and and_4 (and_4_out, C2_out, not_2_out, not_1_out, A4_out);
  or or_1 (or_1_out, and_1_out, and_2_out, and_3_out, and_4_out, and_5_out, and_6_out, and_7_out, and_8_out);
  LED C0ut (.in(or_1_out));
  Button A3 (.out(A3_out));
  and and_5 (and_5_out, not_3_out, C1_out, C0_out, A3_out);
  and and_6 (and_6_out, not_3_out, C1_out, not_1_out, A2_out);
  Button A2 (.out(A2_out));
  and and_7 (and_7_out, not_3_out, not_2_out, C0_out, A1_out);
  Button A1 (.out(A1_out));
  and and_8 (and_8_out, not_3_out, not_2_out, not_1_out, A0_out);
  Button A0 (.out(A0_out));
  LED led_1 (.in(C0_out));
  LED led_2 (.in(not_1_out));
  LED led_3 (.in(C1_out));
  LED led_4 (.in(not_2_out));
  LED led_5 (.in(C2_out));
  LED led_6 (.in(not_3_out));
endmodule

module CarrySaveAdder (
  input  [3:0] in_1,
  input  [3:0] in_2,
  output [3:0] Sum,
  output Overflow
);

  wire fulladder_1_cout, fulladder_2_cout, fulladder_3_cout;

  FullAdder fulladder_1 (.Cin(1'b0), .A(in_1[0]), .B(in_2[0]), .Sout(Sum[0]), .Cout(fulladder_1_cout));
  FullAdder fulladder_2 (.Cin(fulladder_1_cout), .A(in_1[1]), .B(in_2[1]), .Sout(Sum[1]), .Cout(fulladder_2_cout));
  FullAdder fulladder_3 (.Cin(fulladder_2_cout), .A(in_1[2]), .B(in_2[2]), .Sout(Sum[2]), .Cout(fulladder_3_cout));
  FullAdder fulladder_4 (.Cin(fulladder_3_cout), .A(in_1[3]), .B(in_2[3]), .Sout(Sum[3]), .Cout(Overflow));

  // Notes on the sheet:
  //   Least
  //   Most
endmodule

module BasicSRFlipFlop (
  input  S,
  input  R,
  output Q,
  output Q2
);

  nand nand_1 (Q, S, Q2);
  nand nand_2 (Q2, Q, R);
endmodule

module DTypeFlipFlop (
  input  S,
  input  Clk,
  output Q1,
  output ClkOut
);

  wire nand_1_out, nand_2_out, not_1_out;

  not not_1 (not_1_out, S);
  nand nand_1 (nand_1_out, S, Clk);
  nand nand_2 (nand_2_out, not_1_out, Clk);
  BasicSRFlipFlop basicsrflipflop_1 (.S(nand_1_out), .R(nand_2_out), .Q(Q1), .Q2(ClkOut));
endmodule

module BitBinaryCounter (
  output Q0,
  output Q1,
  output Q2,
  output Q3
);

  wire clock_1_out, dtypeflipflop_1_clkout, dtypeflipflop_2_clkout, dtypeflipflop_3_clkout,
       dtypeflipflop_4_clkout;

  Clock clock_1 (.out(clock_1_out));
  DTypeFlipFlop dtypeflipflop_1 (
    .S(dtypeflipflop_1_clkout), .Clk(clock_1_out), .Q1(Q0), .ClkOut(dtypeflipflop_1_clkout));
  DTypeFlipFlop dtypeflipflop_2 (
    .S(dtypeflipflop_2_clkout), .Clk(dtypeflipflop_1_clkout), .Q1(Q1), .ClkOut(dtypeflipflop_2_clkout));
  DTypeFlipFlop dtypeflipflop_3 (
    .S(dtypeflipflop_3_clkout), .Clk(dtypeflipflop_2_clkout), .Q1(Q2), .ClkOut(dtypeflipflop_3_clkout));
  DTypeFlipFlop dtypeflipflop_4 (
    .S(dtypeflipflop_4_clkout), .Clk(dtypeflipflop_3_clkout), .Q1(Q3), .ClkOut(dtypeflipflop_4_clkout));

  // Notes on the sheet:
  //   4 bits
endmodule

module Sequencer (
  input  X0,
  input  X1,
  input  X2,
  input  A7,
  input  A6,
  input  A5,
  input  A4,
  input  A3,
  input  A2,
  input  A1,
  input  A0,
  output O_0,
  output O_1,
  output O_2,
  output O_3,
  output O_4,
  output O_5
);

  wire clock_1_out, d_ff_1_qn, d_ff_2_qn, d_ff_3_qn;

  D_Flip_Flop d_ff_1 (.D(d_ff_1_qn), .clk(clock_1_out), .Q(X0), .Qn(d_ff_1_qn));  // open: preset, reset
  Clock #(.phaseOffset(10)) clock_1 (.out(clock_1_out));
  D_Flip_Flop d_ff_2 (.D(d_ff_2_qn), .clk(d_ff_1_qn), .Q(X1), .Qn(d_ff_2_qn));  // open: preset, reset
  D_Flip_Flop d_ff_3 (.D(d_ff_3_qn), .clk(d_ff_2_qn), .Q(X2), .Qn(d_ff_3_qn));  // open: preset, reset
  Decoder3Bit decoder3bit_1 (
    .C1(d_ff_1_qn), .C2(d_ff_2_qn), .C3(d_ff_3_qn), .A7(A7), .A6(A6), .A5(A5), .A4(A4), .A3(A3), .A2(A2),
    .A1(A1), .A0(A0), .O_0(O_0), .O_1(O_1), .O_2(O_2), .O_3(O_3), .O_4(O_4), .O_5(O_5));
endmodule
