// Logisim project ManchesterBaby.circ as structural Verilog: 4 circuits, main circuit main
module main (
);

  wire and_1_out, and_2_out, and_3_out, and_4_out, and_5_out, and_6_out, and_7_out, and_8_out, and_9_out,
       and_10_out, and_11_out, and_12_out, Clk, comparator_1_lt, decoder_1_out4, decoder_1_out5, HLT, JMP,
       JRP, LDN, or_2_out, or_4_out, or_6_out, or_7_out, s_r_ff_1_q, s_r_ff_1_qn, SKN, STO, SUB, t0, t1, t2,
       t3, t4, t5, t6, t7;
  wire [2:0] counter_1_q;
  wire [4:0] adder_1_out, adder_2_out, adder_3_out, multiplexer_3_out, multiplexer_4_out, multiplexer_5_out,
       multiplexer_6_out, multiplexer_7_out, multiplexer_8_out, multiplexer_9_out, multiplexer_10_out,
       multiplexer_11_out, multiplexer_12_out, or_5_out, or_8_out, PC_q;
  wire [4:1] undriven;
  wire [31:0] Acc_q, IR_q, multiplexer_1_out, multiplexer_2_out, or_1_out, ram_1_dout, subtractor_1_out,
       subtractor_2_out;

  Clock clock_1 (.out(Clk));
  Subtractor #(.width(32)) subtractor_1 (.a({32{1'b0}}), .b(ram_1_dout), .out(subtractor_1_out));  // open: bin, bout
  Subtractor #(.width(32)) subtractor_2 (.a(Acc_q), .b(ram_1_dout), .out(subtractor_2_out));  // open: bin, bout
  Register #(.width(32)) IR (.D(ram_1_dout), .en(t2), .clk(Clk), .Q(IR_q));  // open: clr
  S_R_Flip_Flop s_r_ff_1 (.S(and_1_out), .R(1'b0), .clk(Clk), .Q(s_r_ff_1_q), .Qn(s_r_ff_1_qn));  // open: reset, preset
  and and_1 (and_1_out, HLT, t4);
  Multiplexer #(.width(32)) multiplexer_1 (
    .in0({32{1'b0}}), .in1(subtractor_1_out), .out(multiplexer_1_out), .sel(and_2_out));
  and and_2 (and_2_out, t4, LDN);
  Multiplexer #(.width(32)) multiplexer_2 (
    .in0({32{1'b0}}), .in1(subtractor_2_out), .out(multiplexer_2_out), .sel(and_3_out));
  and and_3 (and_3_out, t4, SUB);
  // Probe on s_r_ff_1_q
  Register #(.width(32)) Acc (.D(or_1_out), .en(or_2_out), .clk(Clk), .Q(Acc_q));  // open: clr
  assign or_1_out = multiplexer_1_out | multiplexer_2_out;  // OR_Gate or_1, 32 bits wide
  or or_2 (or_2_out, and_2_out, and_3_out);
  Decoder #(.select(3)) decoder_1 (
    .out0(JMP), .out1(JRP), .out2(LDN), .out3(STO), .out4(decoder_1_out4), .out5(decoder_1_out5), .out6(SKN),
    .out7(HLT), .sel(IR_q[15:13]));  // open: en
  or or_3 (SUB, decoder_1_out4, decoder_1_out5);
  Counter #(.max('h7), .width(3)) counter_1 (.clk(and_4_out), .Q(counter_1_q));  // open: clr, load, up, count, D, carry
  and and_4 (and_4_out, Clk, s_r_ff_1_qn);
  Comparator #(.width(32)) comparator_1 (.a(Acc_q), .b({32{1'b0}}), .lt(comparator_1_lt));  // open: gt, eq
  Adder #(.width(5)) adder_1 (.a(ram_1_dout[4:0]), .b(PC_q), .out(adder_1_out));  // open: cin, cout
  or or_4 (or_4_out, SUB, LDN, STO);
  Decoder #(.select(3)) decoder_2 (
    .out0(t0), .out1(t1), .out2(t2), .out3(t3), .out4(t4), .out5(t5), .out6(t6), .out7(t7), .sel(counter_1_q));  // open: en
  Adder #(.width(5)) adder_2 (.a(5'b00001), .b(PC_q), .out(adder_2_out));  // open: cin, cout
  Adder #(.width(5)) adder_3 (.a(ram_1_dout[4:0]), .b({undriven, 1'b0}), .out(adder_3_out));  // open: cin, cout
  and and_5 (and_5_out, SKN, t5);
  Multiplexer #(.width(5)) multiplexer_3 (.in0({5{1'b0}}), .in1(adder_1_out), .out(multiplexer_3_out), .sel(and_6_out));
  and and_6 (and_6_out, JRP, t5);
  Multiplexer #(.width(5)) multiplexer_4 (.in0({5{1'b0}}), .in1(PC_q), .out(multiplexer_4_out), .sel(and_7_out));
  and and_7 (and_7_out, or_4_out, t5);
  Multiplexer #(.width(5)) multiplexer_5 (.in0({5{1'b0}}), .in1(adder_2_out), .out(multiplexer_5_out), .sel(t0));
  Multiplexer #(.width(5)) multiplexer_6 (
    .in0({5{1'b0}}), .in1(ram_1_dout[4:0]), .out(multiplexer_6_out), .sel(and_8_out));
  and and_8 (and_8_out, JMP, t5);
  Multiplexer #(.width(5)) multiplexer_7 (.in0({5{1'b0}}), .in1(adder_3_out), .out(multiplexer_7_out), .sel(and_5_out));
  assign or_5_out = multiplexer_5_out | multiplexer_6_out | multiplexer_7_out | multiplexer_3_out | multiplexer_4_out;  // OR_Gate or_5, 5 bits wide
  Register #(.width(5)) PC (.D(or_5_out), .en(or_6_out), .clk(Clk), .Q(PC_q));  // open: clr
  or or_6 (or_6_out, t0, t5);
  and and_9 (and_9_out, t3, LDN);
  or or_7 (or_7_out, JMP, JRP);
  Multiplexer #(.width(5)) multiplexer_8 (.in0({5{1'b0}}), .in1(PC_q), .out(multiplexer_8_out), .sel(t1));
  Multiplexer #(.width(5)) multiplexer_9 (.in0({5{1'b0}}), .in1(IR_q[4:0]), .out(multiplexer_9_out), .sel(and_9_out));
  Multiplexer #(.width(5)) multiplexer_10 (
    .in0({5{1'b0}}), .in1(IR_q[4:0]), .out(multiplexer_10_out), .sel(and_10_out));
  and and_10 (and_10_out, t3, STO);
  Multiplexer #(.width(5)) multiplexer_11 (
    .in0({5{1'b0}}), .in1(IR_q[4:0]), .out(multiplexer_11_out), .sel(and_11_out));
  and and_11 (and_11_out, t3, SUB);
  Multiplexer #(.width(5)) multiplexer_12 (
    .in0({5{1'b0}}), .in1(IR_q[4:0]), .out(multiplexer_12_out), .sel(and_12_out));
  and and_12 (and_12_out, t4, or_7_out);
  assign or_8_out = multiplexer_8_out | multiplexer_9_out | multiplexer_10_out | multiplexer_11_out | multiplexer_12_out;  // OR_Gate or_8, 5 bits wide
  RAM #(.addrWidth(5), .dataWidth(32)) ram_1 (
    .addr(or_8_out), .we(and_10_out), .oe(1'b1), .clk(Clk), .din(Acc_q), .dout(ram_1_dout));
endmodule

module BabyRegister (
  input  in_1,
  input  in_2,
  input  in_3,
  input  clk,
  output [2:0] out_5
);

  D_Flip_Flop d_ff_1 (.D(in_1), .clk(clk), .Q(out_5[0]));  // open: Qn, preset, reset
  D_Flip_Flop d_ff_2 (.D(in_2), .clk(clk), .Q(out_5[1]));  // open: Qn, preset, reset
  D_Flip_Flop d_ff_3 (.D(in_3), .clk(clk), .Q(out_5[2]));  // open: Qn, preset, reset
endmodule

module BabyALU (
  input  [31:0] b,
  input  [31:0] a,
  input  [1:0] C,
  output [31:0] r,
  output f
);

  wire decoder_1_out0, decoder_1_out1, decoder_1_out2, decoder_1_out3;
  wire [31:0] adder_1_out, divider_1_out, multiplexer_1_out, multiplexer_2_out, multiplexer_3_out,
       multiplexer_4_out, multiplier_1_out, subtractor_1_out;

  Adder #(.width(32)) adder_1 (.a(b), .b(a), .out(adder_1_out));  // open: cin, cout
  Multiplier #(.width(32)) multiplier_1 (.a(b), .b(a), .out(multiplier_1_out));  // open: cin, cout
  Subtractor #(.width(32)) subtractor_1 (.a(b), .b(a), .out(subtractor_1_out));  // open: bin, bout
  Divider #(.width(32)) divider_1 (.a(b), .b(a), .out(divider_1_out));  // open: upper, rem
  Decoder #(.select(2)) decoder_1 (
    .out0(decoder_1_out0), .out1(decoder_1_out1), .out2(decoder_1_out2), .out3(decoder_1_out3), .sel(C));  // open: en
  Multiplexer #(.width(32)) multiplexer_1 (
    .in0({32{1'b0}}), .in1(adder_1_out), .out(multiplexer_1_out), .sel(decoder_1_out0));
  Multiplexer #(.width(32)) multiplexer_2 (
    .in0({32{1'b0}}), .in1(multiplier_1_out), .out(multiplexer_2_out), .sel(decoder_1_out1));
  Multiplexer #(.width(32)) multiplexer_3 (
    .in0({32{1'b0}}), .in1(subtractor_1_out), .out(multiplexer_3_out), .sel(decoder_1_out2));
  Multiplexer #(.width(32)) multiplexer_4 (
    .in0({32{1'b0}}), .in1(divider_1_out), .out(multiplexer_4_out), .sel(decoder_1_out3));
  assign r = multiplexer_1_out | multiplexer_2_out | multiplexer_3_out | multiplexer_4_out;  // OR_Gate or_1, 32 bits wide
  Comparator #(.width(32)) comparator_1 (.a(r), .b({32{1'b0}}), .eq(f));  // open: gt, lt
endmodule

module BabyCU3Bit (
  input  [31:0] in_1,
  input  [31:0] in_2,
  input  [31:0] in_3,
  input  [31:0] in_4,
  output [31:0] out_5,
  output [31:0] out_6,
  output [31:0] out_7
);

  wire and_1_out, and_2_out, clock_1_out, d_ff_1_qn, d_ff_2_qn, d_ff_3_qn, decoder_1_out0, decoder_1_out1,
       decoder_1_out7, switch_1_p1, switch_2_p1;
  wire [2:0] d_ff_1_q;
  wire [31:0] multiplexer_2_out, multiplexer_4_out;

  Clock clock_1 (.out(clock_1_out));
  D_Flip_Flop d_ff_1 (.D(d_ff_1_qn), .clk(clock_1_out), .Q(d_ff_1_q[0]), .Qn(d_ff_1_qn));  // open: preset, reset
  D_Flip_Flop d_ff_2 (.D(d_ff_2_qn), .clk(d_ff_1_qn), .Q(d_ff_1_q[1]), .Qn(d_ff_2_qn));  // open: preset, reset
  D_Flip_Flop d_ff_3 (.D(d_ff_3_qn), .clk(d_ff_2_qn), .Q(d_ff_1_q[2]), .Qn(d_ff_3_qn));  // open: preset, reset
  // Switch switch_1: pin names not known; wires that end beside it: switch_1_p1
  Decoder #(.select(3)) decoder_1 (
    .out0(decoder_1_out0), .out1(decoder_1_out1), .out7(decoder_1_out7), .sel(d_ff_1_q));  // open: out2, out3, out4, out5, out6, en
  // Switch switch_2: pin names not known; wires that end beside it: switch_2_p1
  and and_1 (and_1_out, decoder_1_out7, switch_1_p1);
  and and_2 (and_2_out, decoder_1_out7, switch_2_p1);
  Multiplexer #(.width(32)) multiplexer_1 (.in0({32{1'b0}}), .in1(in_1), .out(out_5), .sel(decoder_1_out0));
  Multiplexer #(.width(32)) multiplexer_2 (.in0({32{1'b0}}), .in1(in_2), .out(multiplexer_2_out), .sel(decoder_1_out1));
  Multiplexer #(.width(32)) multiplexer_3 (.in0({32{1'b0}}), .in1(in_3), .out(out_7), .sel(and_1_out));
  Multiplexer #(.width(32)) multiplexer_4 (.in0({32{1'b0}}), .in1(in_4), .out(multiplexer_4_out), .sel(and_2_out));
  assign out_6 = multiplexer_2_out | multiplexer_4_out;  // OR_Gate or_1, 32 bits wide
endmodule
