// Logisim project PC_Architecture.circ as structural Verilog: 2 circuits, main circuit main
module main (
);

  DirectMapped directmapped_1 ();  // open: A_FSB, D_RAM, A_RAM, D_FSB
endmodule

module DirectMapped (
  input  [15:0] A_FSB,
  input  [31:0] D_RAM,
  output [15:0] A_RAM,
  output [31:0] D_FSB
);

  wire comparator_1_eq, not_1_out;
  wire [47:0] ram_1_dout;

  RAM #(.dataWidth(48)) ram_1 (
    .addr(A_FSB[7:0]), .we(not_1_out), .din({D_FSB, A_FSB}), .dout(ram_1_dout));  // open: oe, clk
  Comparator #(.width(16)) comparator_1 (.a(A_FSB), .b(ram_1_dout[15:0]), .eq(comparator_1_eq));  // open: gt, lt
  not not_1 (not_1_out, comparator_1_eq);
  Multiplexer #(.width(32)) multiplexer_1 (.in0(ram_1_dout[47:16]), .in1(D_RAM), .out(D_FSB), .sel(comparator_1_eq));

  assign A_RAM = A_FSB;
endmodule
